// Logisim project memoria_rom.circ as structural Verilog: 1 circuit, main circuit main
module main (
  input  habilitar,
  input  [1:0] endereco
);

  wire decoder_1_out0, decoder_1_out1, decoder_1_out2, decoder_1_out3, or_1_out, or_2_out, or_3_out, or_4_out;

  Decoder #(.select(2)) decoder_1 (
    .out0(decoder_1_out0), .out1(decoder_1_out1), .out2(decoder_1_out2), .out3(decoder_1_out3),
    .sel(endereco), .en(habilitar));
  or or_1 (or_1_out, decoder_1_out1, decoder_1_out2);
  LED led_1 (.in(or_1_out));
  or or_2 (or_2_out, decoder_1_out0, decoder_1_out2);
  LED led_2 (.in(or_2_out));
  or or_3 (or_3_out, decoder_1_out2, decoder_1_out1);
  LED led_3 (.in(or_3_out));
  or or_4 (or_4_out, decoder_1_out1, decoder_1_out0);
  LED led_4 (.in(or_4_out));
endmodule
